// Logisim project 6.crc.circ as structural Verilog: 1 circuit, main circuit main
module main (
  input  A,
  input  B,
  input  C,
  input  D,
  output out_5
);

  wire A_prime_out, and_1_out, and_2_out, and_3_out, and_4_out, and_5_out, and_6_out, and_7_out, B_prime_out,
       C_prime_out, D_prime_out, m0_out;

  not A_prime (A_prime_out, A);
  not B_prime (B_prime_out, B);
  not C_prime (C_prime_out, C);
  not D_prime (D_prime_out, D);
  and m0 (m0_out, A_prime_out, B_prime_out, C_prime_out, D_prime_out);
  and and_1 (and_1_out, A_prime_out, B_prime_out, C, D_prime_out);
  and and_2 (and_2_out, A_prime_out, B, C_prime_out, D);
  and and_3 (and_3_out, A_prime_out, B, C, D);
  and and_4 (and_4_out, A, B_prime_out, C_prime_out, D_prime_out);
  and and_5 (and_5_out, A, C_prime_out, C, D_prime_out);
  and and_6 (and_6_out, A, B_prime_out, C_prime_out, D);
  and and_7 (and_7_out, A, B, C, D);
  or or_1 (out_5, m0_out, and_1_out, and_2_out, and_3_out, and_4_out, and_5_out, and_6_out, and_7_out);
endmodule
