// Logisim project DL 3.circ as structural Verilog: 1 circuit, main circuit main
module main (
  input  A,
  input  A_2,
  input  B,
  input  A_3,
  input  B_2,
  output out_6,
  output out_7,
  output out_8
);

  wire nor_1_out, nor_3_out, nor_4_out;

  nor nor_1 (nor_1_out, A_2, B);
  nor nor_2 (out_6, A, A);
  nor nor_3 (nor_3_out, A_3, A_3);
  nor nor_4 (nor_4_out, B_2, B_2);
  nor nor_5 (out_7, nor_1_out, nor_1_out);
  nor nor_6 (out_8, nor_3_out, nor_4_out);
endmodule
