// Logisim project DL 4.circ as structural Verilog: 1 circuit, main circuit main
module main (
  input  A,
  input  B,
  input  A_2,
  input  B_2,
  input  in_5,
  input  in_6,
  input  A_3,
  input  B_3,
  output out_9,
  output out_10,
  output out_11,
  output out_12
);

  wire and_1_out, not_1_out, not_2_out, not_3_out, not_4_out, or_1_out;

  or or_1 (or_1_out, A, B);
  not not_1 (not_1_out, A_2);
  not not_2 (not_2_out, B_2);
  and and_1 (and_1_out, in_5, in_6);
  not not_3 (not_3_out, A_3);
  not not_4 (not_4_out, B_3);
  not not_5 (out_9, or_1_out);
  and and_2 (out_10, not_1_out, not_2_out);
  not not_6 (out_11, and_1_out);
  or or_2 (out_12, not_3_out, not_4_out);
endmodule
