// Logisim project DL 8.circ as structural Verilog: 1 circuit, main circuit main
module main (
  input  A,
  input  B,
  input  cin
);

  wire and_1_out, and_2_out, or_1_out, xor_1_out, xor_2_out;

  xor xor_1 (xor_1_out, A, B);
  xor xor_2 (xor_2_out, xor_1_out, cin);
  and and_1 (and_1_out, xor_1_out, cin);
  and and_2 (and_2_out, A, B);
  LED sum (.in(xor_2_out));
  or or_1 (or_1_out, and_1_out, and_2_out);
  LED carry (.in(or_1_out));
endmodule
