// Logisim project dl.3..circ as structural Verilog: 1 circuit, main circuit main
module main (
  input  in_1,
  input  in_2,
  input  in_3,
  input  in_4,
  input  in_5,
  input  in_6,
  input  in_7,
  output out_8
);

  wire nor_1_out, nor_2_out, nor_4_out, nor_5_out, nor_6_out;

  nor nor_1 (nor_1_out, in_6, in_7);
  nor nor_2 (nor_2_out, in_1, in_1);
  not nor_3 (out_8, nor_1_out);  // NOR_Gate
  nor nor_4 (nor_4_out, in_2, in_2);
  nor nor_5 (nor_5_out, in_5, in_5);
  nor nor_6 (nor_6_out, nor_4_out, nor_5_out);
endmodule
