// Logisim project dl.lab.01.circ as structural Verilog: 1 circuit, main circuit main
module main (
  input  a,
  input  b,
  input  a_2,
  input  b_2,
  input  a_3,
  input  a_4,
  input  b_3,
  input  a_5,
  input  b_4,
  output y,
  output y_2,
  output y_3,
  output y_4,
  output y_5
);

  and and_1 (y, a, b);
  or or_1 (y_2, a_2, b_2);
  not not_1 (y_3, a_3);
  xor xor_1 (y_4, a_4, b_3);
  xnor xnor_1 (y_5, a_5, b_4);
endmodule
